// Logisim project nand2tetrisP1.circ as structural Verilog: 16 circuits, main circuit main
module main (
  input  in_1,
  input  in_2,
  output [6:0] out_3,
  output [15:0] out_4,
  output [14:0] out_5,
  output [15:0] out_6,
  output [15:0] out_7,
  output [14:0] out_8,
  output [15:0] out_9,
  output [15:0] out_10,
  output [15:0] out_11,
  output [15:0] out_12
);

  wire and_1_out, button_1_out, clock_1_out, clock_2_out, cpu_1_writem, demultiplexer_1_out0,
       demultiplexer_1_out1, not_1_out, or_1_out, or_2_out;
  wire [6:0] adder_2_out, adder_3_out, X_q, Y_q;
  wire [13:0] adder_1_out, bit_extender_1_out, multiplexer_1_out, register_1_q;

  ROM #(.addrWidth(15), .dataWidth(16)) rom_1 (.addr(out_8), .data(out_10));
  Button button_1 (.out(button_1_out));
  Clock clock_1 (.out(clock_1_out));
  or or_1 (or_1_out, button_1_out, in_2);
  CPU cpu_1 (
    .instruction(out_10), .inM(out_12), .clk(clock_1_out), .res(or_1_out), .dD(out_4), .outM(out_9),
    .dA(out_6), .address(out_5), .writeM(cpu_1_writem), .pcval(out_8));
  Demultiplexer demultiplexer_1 (
    .out0(demultiplexer_1_out0), .out1(demultiplexer_1_out1), .in(cpu_1_writem), .sel(out_5[14]));
  Bit_Extender #(.in_width(15), .out_width(14)) bit_extender_1 (.in(out_5), .out(bit_extender_1_out));
  RAM #(.addrWidth(14), .dataWidth(16)) ram_1 (
    .addr(bit_extender_1_out), .we(demultiplexer_1_out0), .oe(1'b1), .clk(clock_1_out), .din(out_9),
    .dout(out_12));
  Adder #(.width(14)) adder_1 (.a(register_1_q), .b(14'h1), .out(adder_1_out));  // open: cin, cout
  Register #(.width(14)) register_1 (
    .D(adder_1_out), .en(and_1_out), .clk(clock_2_out), .Q(register_1_q), .clr(or_2_out));
  Clock clock_2 (.out(clock_2_out));
  Multiplexer #(.width(14)) multiplexer_1 (
    .in0(register_1_q), .in1(bit_extender_1_out), .out(multiplexer_1_out), .sel(demultiplexer_1_out1));
  not not_1 (not_1_out, demultiplexer_1_out1);
  and and_1 (and_1_out, 1'b1, not_1_out);
  Adder #(.width(7)) adder_2 (.a(X_q), .b(7'b0000001), .out(adder_2_out), .cout(out_3[0]));  // open: cin
  Adder #(.width(7)) adder_3 (.a(Y_q), .b({{6{1'b0}}, out_3[0]}), .out(adder_3_out));  // open: cin, cout
  RAM #(.addrWidth(14), .dataWidth(16)) ram_2 (
    .addr(multiplexer_1_out), .we(demultiplexer_1_out1), .oe(1'b1), .clk(clock_2_out), .din(out_9),
    .dout(out_11));
  Register #(.width(7)) X (.D(adder_2_out), .en(and_1_out), .clk(clock_2_out), .Q(X_q), .clr(or_2_out));
  Register #(.width(7)) Y (.D(adder_3_out), .en(and_1_out), .clk(clock_2_out), .Q(Y_q), .clr(or_2_out));
  or or_2 (or_2_out, in_1, or_1_out);
  // RGB_Video rgb_video_1: pin names not known; wires that end beside it: or_2_out, clock_2_out, and_1_out, X_q, Y_q, out_11

  assign out_3[6:1] = {6{1'b0}};
  assign out_7 = out_6;

  // Notes on the sheet:
  //   contents of rom_1 (hex, n*v repeats v):
  //   4010 ec10 a e308 a fc20 ee88 dada fdc8 4
endmodule

module and16 (
  input  a,
  input  a_1,
  input  a_2,
  input  a_3,
  input  a_4,
  input  a_5,
  input  a_6,
  input  a_7,
  input  a_8,
  input  a_9,
  input  a_10,
  input  a_11,
  input  a_12,
  input  a_13,
  input  a_14,
  input  a_15,
  input  b,
  input  b_1,
  input  b_2,
  input  b_3,
  input  b_4,
  input  b_5,
  input  b_6,
  input  b_7,
  input  b_8,
  input  b_9,
  input  b_10,
  input  b_11,
  input  b_12,
  input  b_13,
  input  b_14,
  input  b_15,
  output o,
  output o_1,
  output o_2,
  output o_3,
  output o_4,
  output o_5,
  output o_6,
  output o_7,
  output o_8,
  output o_9,
  output o_10,
  output o_11,
  output o_12,
  output o_13,
  output o_14,
  output o_15
);

  and and_1 (o, a, b);
  and and_2 (o_1, a_1, b_1);
  and and_3 (o_2, a_2, b_2);
  and and_4 (o_3, a_3, b_3);
  and and_5 (o_4, a_4, b_4);
  and and_6 (o_5, a_5, b_5);
  and and_7 (o_6, a_6, b_6);
  and and_8 (o_7, a_7, b_7);
  and and_9 (o_8, a_8, b_8);
  and and_10 (o_9, a_9, b_9);
  and and_11 (o_10, a_10, b_10);
  and and_12 (o_11, a_11, b_11);
  and and_13 (o_12, a_12, b_12);
  and and_14 (o_13, a_13, b_13);
  and and_15 (o_14, a_14, b_14);
  and and_16 (o_15, a_15, b_15);
endmodule

module mux16 (
  input  [15:0] a,
  input  [15:0] b,
  input  sel,
  output [15:0] o
);

  Multiplexer #(.width(16)) multiplexer_1 (.in0(a), .in1(b), .out(o), .sel(sel));
endmodule

module mux4way16 (
  input  [15:0] a,
  input  [15:0] a_1,
  input  [15:0] a_2,
  input  [15:0] a_3,
  input  [1:0] sel,
  output [15:0] o
);

  wire [15:0] multiplexer_1_out, multiplexer_2_out;

  Multiplexer #(.width(16)) multiplexer_1 (.in0(a), .in1(a_2), .out(multiplexer_1_out), .sel(sel[1]));
  Multiplexer #(.width(16)) multiplexer_2 (.in0(a_1), .in1(a_3), .out(multiplexer_2_out), .sel(sel[1]));
  Multiplexer #(.width(16)) multiplexer_3 (.in0(multiplexer_1_out), .in1(multiplexer_2_out), .out(o), .sel(sel[0]));
endmodule

module add3r (
  input  resin,
  input  a,
  input  b,
  output o,
  output res
);

  wire and_1_out, and_2_out, xor_1_out;

  and and_1 (and_1_out, a, b);
  xor xor_1 (xor_1_out, a, b);
  and and_2 (and_2_out, xor_1_out, resin);
  xor xor_2 (o, xor_1_out, resin);
  or or_1 (res, and_1_out, and_2_out);
endmodule

module adder16 (
  input  [15:0] a,
  input  [15:0] b,
  output [15:0] o
);

  wire adder_1_cout, adder_2_cout, adder_3_cout, adder_4_cout, adder_5_cout, adder_6_cout, adder_7_cout,
       adder_8_cout, adder_9_cout, adder_10_cout, adder_11_cout, adder_12_cout, adder_13_cout, adder_14_cout,
       adder_15_cout;

  Adder #(.width(1)) adder_1 (.a(a[0]), .b(b[0]), .out(o[0]), .cout(adder_1_cout));  // open: cin
  Adder #(.width(1)) adder_2 (.a(a[1]), .b(b[1]), .out(o[1]), .cin(adder_1_cout), .cout(adder_2_cout));
  Adder #(.width(1)) adder_3 (.a(a[2]), .b(b[2]), .out(o[2]), .cin(adder_2_cout), .cout(adder_3_cout));
  Adder #(.width(1)) adder_4 (.a(a[3]), .b(b[3]), .out(o[3]), .cin(adder_3_cout), .cout(adder_4_cout));
  Adder #(.width(1)) adder_5 (.a(a[4]), .b(b[4]), .out(o[4]), .cin(adder_4_cout), .cout(adder_5_cout));
  Adder #(.width(1)) adder_6 (.a(a[5]), .b(b[5]), .out(o[5]), .cin(adder_5_cout), .cout(adder_6_cout));
  Adder #(.width(1)) adder_7 (.a(a[6]), .b(b[6]), .out(o[6]), .cin(adder_6_cout), .cout(adder_7_cout));
  Adder #(.width(1)) adder_8 (.a(a[7]), .b(b[7]), .out(o[7]), .cin(adder_7_cout), .cout(adder_8_cout));
  Adder #(.width(1)) adder_9 (.a(a[8]), .b(b[8]), .out(o[8]), .cin(adder_8_cout), .cout(adder_9_cout));
  Adder #(.width(1)) adder_10 (.a(a[9]), .b(b[9]), .out(o[9]), .cin(adder_9_cout), .cout(adder_10_cout));
  Adder #(.width(1)) adder_11 (.a(a[10]), .b(b[10]), .out(o[10]), .cin(adder_10_cout), .cout(adder_11_cout));
  Adder #(.width(1)) adder_12 (.a(a[11]), .b(b[11]), .out(o[11]), .cin(adder_11_cout), .cout(adder_12_cout));
  Adder #(.width(1)) adder_13 (.a(a[12]), .b(b[12]), .out(o[12]), .cin(adder_12_cout), .cout(adder_13_cout));
  Adder #(.width(1)) adder_14 (.a(a[13]), .b(b[13]), .out(o[13]), .cin(adder_13_cout), .cout(adder_14_cout));
  Adder #(.width(1)) adder_15 (.a(a[14]), .b(b[14]), .out(o[14]), .cin(adder_14_cout), .cout(adder_15_cout));
  Adder #(.width(1)) adder_16 (.a(a[15]), .b(b[15]), .out(o[15]), .cin(adder_15_cout));  // open: cout
endmodule

module sub16 (
  input  [15:0] a,
  input  [15:0] b,
  output [15:0] o
);

  wire [15:0] adder16_1_o, not_1_out;

  assign not_1_out = ~b;  // NOT_Gate not_1, 16 bits wide
  adder16 adder16_1 (.o(adder16_1_o));  // open: a, b
  adder16 adder16_2 (.o(o));  // open: a, b
endmodule

module inc16 (
  input  [15:0] a,
  output [15:0] o
);

  adder16 adder16_1 (.o(o));  // open: a, b
endmodule

module alu (
  input  no,
  input  zx,
  input  nx,
  input  zy,
  input  ny,
  input  f,
  input  [15:0] x,
  input  [15:0] y,
  output [15:0] o,
  output out_10,
  output zr,
  output ng
);

  wire [15:0] adder16_1_o, and_1_out, and_2_out, and_3_out, bit_extender_1_out, bit_extender_2_out,
       bit_extender_3_out, bit_extender_4_out, bit_extender_5_out, multiplexer_1_out, not_1_out, not_2_out,
       xor_1_out, xor_2_out;

  assign bit_extender_1_out = {{15{zx}}, zx};  // Bit_Extender bit_extender_1
  assign not_1_out = ~bit_extender_1_out;  // NOT_Gate not_1, 16 bits wide
  assign and_1_out = not_1_out & x;  // AND_Gate and_1, 16 bits wide
  assign bit_extender_2_out = {{15{zy}}, zy};  // Bit_Extender bit_extender_2
  assign bit_extender_3_out = {{15{nx}}, nx};  // Bit_Extender bit_extender_3
  assign not_2_out = ~bit_extender_2_out;  // NOT_Gate not_2, 16 bits wide
  assign and_2_out = not_2_out & y;  // AND_Gate and_2, 16 bits wide
  assign xor_1_out = bit_extender_3_out ^ and_1_out;  // XOR_Gate xor_1, 16 bits wide
  assign bit_extender_4_out = {{15{ny}}, ny};  // Bit_Extender bit_extender_4
  assign xor_2_out = bit_extender_4_out ^ and_2_out;  // XOR_Gate xor_2, 16 bits wide
  assign and_3_out = xor_1_out & xor_2_out;  // AND_Gate and_3, 16 bits wide
  adder16 adder16_1 (.a(xor_1_out), .b(xor_2_out), .o(adder16_1_o));
  Multiplexer #(.width(16)) multiplexer_1 (.in0(and_3_out), .in1(adder16_1_o), .out(multiplexer_1_out), .sel(f));
  assign bit_extender_5_out = {{15{no}}, no};  // Bit_Extender bit_extender_5
  assign {ng, o[14:0]} = bit_extender_5_out ^ multiplexer_1_out;  // XOR_Gate xor_3, 16 bits wide
  or16out1 or16out1_1 (.in_1({ng, o[14:0]}), .out_2(out_10));
  not not_3 (zr, out_10);

  assign o[15] = ng;

  // Notes on the sheet:
  //   x&y
  //   x+y
endmodule

module Bit (
  input  load,
  input  d,
  output o
);

  wire clock_1_out, multiplexer_1_out, not_1_out;

  not not_1 (not_1_out, load);
  D_Flip_Flop d_ff_1 (.D(multiplexer_1_out), .clk(clock_1_out), .Q(o));  // open: Qn, preset, reset
  Multiplexer multiplexer_1 (.in0(d), .in1(o), .out(multiplexer_1_out), .sel(not_1_out));
  Clock clock_1 (.out(clock_1_out));
endmodule

module RAM8 (
  input  load,
  input  a,
  input  [2:0] addr,
  input  clk,
  output out_5
);

  wire demultiplexer_1_out0, demultiplexer_1_out1, demultiplexer_2_out0, demultiplexer_2_out1,
       demultiplexer_3_out0, demultiplexer_3_out1, demultiplexer_4_out0, demultiplexer_4_out1,
       demultiplexer_5_out0, demultiplexer_5_out1, demultiplexer_6_out0, demultiplexer_6_out1,
       demultiplexer_7_out0, demultiplexer_7_out1, multiplexer_1_out, multiplexer_2_out, multiplexer_3_out,
       multiplexer_5_out, multiplexer_6_out, multiplexer_7_out, register_1_q, register_2_q, register_3_q,
       register_4_q, register_5_q, register_6_q, register_7_q, register_8_q;

  Demultiplexer demultiplexer_1 (.out0(demultiplexer_1_out0), .out1(demultiplexer_1_out1), .in(load), .sel(addr[2]));
  Demultiplexer demultiplexer_2 (
    .out0(demultiplexer_2_out0), .out1(demultiplexer_2_out1), .in(demultiplexer_3_out0), .sel(addr[0]));
  Demultiplexer demultiplexer_3 (
    .out0(demultiplexer_3_out0), .out1(demultiplexer_3_out1), .in(demultiplexer_1_out0), .sel(addr[1]));
  Demultiplexer demultiplexer_4 (
    .out0(demultiplexer_4_out0), .out1(demultiplexer_4_out1), .in(demultiplexer_3_out1), .sel(addr[0]));
  Demultiplexer demultiplexer_5 (
    .out0(demultiplexer_5_out0), .out1(demultiplexer_5_out1), .in(demultiplexer_6_out0), .sel(addr[0]));
  Demultiplexer demultiplexer_6 (
    .out0(demultiplexer_6_out0), .out1(demultiplexer_6_out1), .in(demultiplexer_1_out1), .sel(addr[1]));
  Demultiplexer demultiplexer_7 (
    .out0(demultiplexer_7_out0), .out1(demultiplexer_7_out1), .in(demultiplexer_6_out1), .sel(addr[0]));
  Register #(.width(1)) register_1 (.D(a), .en(demultiplexer_2_out0), .clk(clk), .Q(register_1_q));  // open: clr
  Register #(.width(1)) register_2 (.D(a), .en(demultiplexer_2_out1), .clk(clk), .Q(register_2_q));  // open: clr
  Register #(.width(1)) register_3 (.D(a), .en(demultiplexer_4_out0), .clk(clk), .Q(register_3_q));  // open: clr
  Register #(.width(1)) register_4 (.D(a), .en(demultiplexer_4_out1), .clk(clk), .Q(register_4_q));  // open: clr
  Register #(.width(1)) register_5 (.D(a), .en(demultiplexer_5_out0), .clk(clk), .Q(register_5_q));  // open: clr
  Register #(.width(1)) register_6 (.D(a), .en(demultiplexer_5_out1), .clk(clk), .Q(register_6_q));  // open: clr
  Register #(.width(1)) register_7 (.D(a), .en(demultiplexer_7_out0), .clk(clk), .Q(register_7_q));  // open: clr
  Register #(.width(1)) register_8 (.D(a), .en(demultiplexer_7_out1), .clk(clk), .Q(register_8_q));  // open: clr
  Multiplexer multiplexer_1 (.in0(register_1_q), .in1(register_2_q), .out(multiplexer_1_out), .sel(addr[0]));
  Multiplexer multiplexer_2 (.in0(multiplexer_1_out), .in1(multiplexer_3_out), .out(multiplexer_2_out), .sel(addr[1]));
  Multiplexer multiplexer_3 (.in0(register_3_q), .in1(register_4_q), .out(multiplexer_3_out), .sel(addr[0]));
  Multiplexer multiplexer_4 (.in0(multiplexer_2_out), .in1(multiplexer_6_out), .out(out_5), .sel(addr[2]));
  Multiplexer multiplexer_5 (.in0(register_5_q), .in1(register_6_q), .out(multiplexer_5_out), .sel(addr[0]));
  Multiplexer multiplexer_6 (.in0(multiplexer_5_out), .in1(multiplexer_7_out), .out(multiplexer_6_out), .sel(addr[1]));
  Multiplexer multiplexer_7 (.in0(register_7_q), .in1(register_8_q), .out(multiplexer_7_out), .sel(addr[0]));
endmodule

module PC (
  input  inc1,
  input  reset,
  input  load,
  input  [14:0] a,
  input  clk,
  output [14:0] o,
  output [15:0] out_7,
  output [14:0] out_8
);

  wire not_1_out, not_2_out;
  wire [14:0] and_1_out, and_2_out, and_3_out, and_4_out, bit_extender_1_out, bit_extender_2_out,
       bit_extender_3_out, multiplexer_1_out;
  wire [15:15] adder16_1_o;

  assign bit_extender_1_out = {{14{load}}, load};  // Bit_Extender bit_extender_1
  not not_1 (not_1_out, load);
  assign and_1_out = bit_extender_1_out & a;  // AND_Gate and_1, 15 bits wide
  not not_2 (not_2_out, reset);
  assign bit_extender_2_out = {{14{not_2_out}}, not_2_out};  // Bit_Extender bit_extender_2
  assign and_2_out = bit_extender_2_out & and_1_out;  // AND_Gate and_2, 15 bits wide
  assign and_3_out = bit_extender_2_out & and_4_out;  // AND_Gate and_3, 15 bits wide
  assign and_4_out = out_8 & bit_extender_3_out;  // AND_Gate and_4, 15 bits wide
  Multiplexer #(.width(15)) multiplexer_1 (.in0(and_2_out), .in1(and_3_out), .out(multiplexer_1_out), .sel(not_1_out));
  assign bit_extender_3_out = {{14{inc1}}, inc1};  // Bit_Extender bit_extender_3
  Register #(.width(15)) register_1 (.D(multiplexer_1_out), .en(1'b1), .clk(clk), .Q(o));  // open: clr
  Clock clock_1 ();  // open: out
  adder16 adder16_1 (.a({1'b0, o}), .b(16'h1), .o({adder16_1_o[15], out_8}));

  assign out_7 = {1'b0, o};
endmodule

module or16out1 (
  input  [15:0] in_1,
  output out_2
);

  wire or_1_out, or_2_out, or_3_out, or_4_out, or_5_out, or_6_out, or_7_out, or_8_out, or_9_out, or_10_out,
       or_11_out, or_12_out, or_13_out, or_15_out;

  or or_1 (or_1_out, in_1[0], in_1[1]);
  or or_2 (or_2_out, in_1[2], in_1[3]);
  or or_3 (or_3_out, in_1[4], in_1[5]);
  or or_4 (or_4_out, in_1[6], in_1[7]);
  or or_5 (or_5_out, in_1[8], in_1[9]);
  or or_6 (or_6_out, in_1[10], in_1[11]);
  or or_7 (or_7_out, in_1[12], in_1[13]);
  or or_8 (or_8_out, in_1[14], in_1[15]);
  or or_9 (or_9_out, or_1_out, or_2_out);
  or or_10 (or_10_out, or_3_out, or_4_out);
  or or_11 (or_11_out, or_5_out, or_6_out);
  or or_12 (or_12_out, or_7_out, or_8_out);
  or or_13 (or_13_out, or_9_out, or_10_out);
  or or_14 (out_2, or_13_out, or_15_out);
  or or_15 (or_15_out, or_11_out, or_12_out);
endmodule

module CPU (
  input  [15:0] instruction,
  input  [15:0] inM,
  input  clk,
  input  res,
  output [15:0] dD,
  output [15:0] outM,
  output [15:0] dA,
  output [14:0] address,
  output writeM,
  output [14:0] pcval
);

  wire alu_1_ng, alu_1_zr, and_1_out, and_2_out, and_3_out, and_4_out, not_1_out, or_1_out, or_2_out;
  wire [2:0] bit_extender_1_out;
  wire [2:1] and_5_out;
  wire [14:0] bit_extender_2_out;
  wire [15:0] multiplexer_1_out, multiplexer_2_out;

  and and_1 (and_1_out, instruction[2], alu_1_ng);
  and and_2 (and_2_out, instruction[0], instruction[1], instruction[2]);
  and and_3 (and_3_out, alu_1_zr, instruction[1]);
  or or_1 (or_1_out, and_2_out, and_2_out, and_3_out, and_1_out);
  assign bit_extender_1_out = {{2{instruction[15]}}, instruction[15]};  // Bit_Extender bit_extender_1
  Multiplexer #(.width(16)) multiplexer_1 (.in0(instruction), .in1(outM), .out(multiplexer_1_out), .sel(and_5_out[2]));
  and and_4 (and_4_out, or_1_out, instruction[15]);
  assign {and_5_out, writeM} = bit_extender_1_out & instruction[5:3];  // AND_Gate and_5, 3 bits wide
  not not_1 (not_1_out, instruction[15]);
  Bit_Extender #(.in_width(16), .out_width(15)) bit_extender_2 (.in(dA), .out(bit_extender_2_out));
  or or_2 (or_2_out, not_1_out, and_5_out[2]);
  PC pc_1 (
    .inc1(1'b1), .reset(res), .load(and_4_out), .a(bit_extender_2_out), .clk(clk), .o(pcval));  // open: out_7, out_8
  Register #(.width(16)) D (.D(outM), .en(and_5_out[1]), .clk(clk), .Q(dD));  // open: clr
  Register #(.width(16)) A (.D(multiplexer_1_out), .en(or_2_out), .clk(clk), .Q(dA));  // open: clr
  Multiplexer #(.width(16)) multiplexer_2 (.in0(dA), .in1(inM), .out(multiplexer_2_out), .sel(instruction[12]));
  alu alu_1 (
    .nx(instruction[10]), .zy(instruction[9]), .ny(instruction[8]), .f(instruction[7]), .no(instruction[6]),
    .x(dD), .y(multiplexer_2_out), .zx(instruction[11]), .zr(alu_1_zr), .o(outM), .ng(alu_1_ng));  // open: out_10
  Bit_Extender #(.in_width(16), .out_width(15)) bit_extender_3 (.in(multiplexer_2_out), .out(address));

  // Notes on the sheet:
  //    1 1 1 a c1 c2 c3 c4 c5 c6 d1 d2 d3 j1 j2 j3 
endmodule

module ogdesign (
  input  in_1,
  input  in_2,
  input  in_3,
  input  in_4,
  input  in_5,
  input  in_6,
  input  [15:0] in_7,
  input  [15:0] in_8,
  input  [14:0] in_9,
  input  [15:0] in_10,
  input  in_11,
  input  clk,
  input  in_13,
  input  in_14,
  input  [15:0] in_15,
  input  in_16,
  output [15:0] out_17,
  output [14:0] out_18,
  output [13:0] out_19,
  output [14:0] out_20,
  output [15:0] out_21,
  output out_22,
  output [15:0] out_23,
  output [15:0] out_24,
  output [15:0] out_25,
  output [14:0] out_26,
  output [14:0] out_27,
  output [15:0] out_28
);

  wire alu_1_ng, alu_1_zr, and_1_out, and_2_out, and_3_out, and_4_out, demultiplexer_1_out0,
       demultiplexer_1_out1, not_1_out, not_2_out, or_2_out, or_3_out;
  wire [13:0] undriven;
  wire [15:0] A_q, D_q, multiplexer_1_out;

  ROM #(.addrWidth(15), .dataWidth(16)) rom_1 (.addr(out_18), .data(out_21));
  // OR_Gate or_1 is placed but not wired
  and and_1 (and_1_out, out_21[0], out_21[1], out_21[2]);
  and and_2 (and_2_out, alu_1_zr, out_21[1]);
  and and_3 (and_3_out, out_21[2], alu_1_ng);
  or or_2 (or_2_out, and_1_out, and_1_out, and_2_out, and_3_out);
  Multiplexer #(.width(16)) multiplexer_1 (.in0(out_21), .in1(out_17), .out(multiplexer_1_out), .sel(out_21[5]));
  and and_4 (and_4_out, or_2_out, out_21[15]);
  not not_1 (not_1_out, clk);
  not not_2 (not_2_out, out_21[15]);
  Bit_Extender #(.in_width(16), .out_width(15)) bit_extender_1 (.in(A_q), .out(out_26));
  Clock clock_1 ();  // open: out
  or or_3 (or_3_out, not_2_out, out_21[5]);
  PC pc_1 (
    .inc1(in_13), .reset(in_14), .load(and_4_out), .a(out_26), .clk(not_1_out), .o(out_18));  // open: out_7, out_8
  Register #(.width(16)) D (.D(out_17), .en(out_21[4]), .clk(clk), .Q(D_q));  // open: clr
  Register #(.width(16)) A (.D(multiplexer_1_out), .en(or_3_out), .clk(clk), .Q(A_q));  // open: clr
  Multiplexer #(.width(16)) multiplexer_2 (.in0(A_q), .in1(out_25), .out(out_23), .sel(out_21[12]));
  Register #(.width(16)) register_1 (.D(in_15), .clk(in_16));  // open: en, Q, clr
  alu alu_1 (
    .nx(out_21[10]), .zy(out_21[9]), .ny(out_21[8]), .f(out_21[7]), .no(out_21[6]), .x(D_q), .y(out_23),
    .zx(out_21[11]), .zr(alu_1_zr), .o(out_17), .ng(alu_1_ng));  // open: out_10
  Demultiplexer demultiplexer_1 (
    .out0(demultiplexer_1_out0), .out1(demultiplexer_1_out1), .in(out_21[3]), .sel(out_23[14]));
  Bit_Extender #(.in_width(16), .out_width(14)) bit_extender_2 (.in(out_23), .out(out_19));
  RAM #(.addrWidth(14), .dataWidth(16)) memory (
    .addr(out_19), .we(demultiplexer_1_out0), .oe(1'b1), .clk(clk), .din(out_17), .dout(out_25));
  RAM #(.addrWidth(14), .dataWidth(16)) video (
    .addr(undriven), .we(demultiplexer_1_out1), .din(out_17), .dout(out_28));  // open: oe, clk
  RAM #(.addrWidth(15), .dataWidth(16)) ram_1 (.addr(in_9));  // open: we, oe, clk, din, dout

  assign out_20 = out_18;
  assign out_22 = out_21[15];
  assign out_24 = out_17;
  assign out_27 = out_18;

  // Notes on the sheet:
  //   contents of rom_1 (hex, n*v repeats v):
  //   a ec10 8 e302 1 e4d0 2 ea87 8 ea87
  //    1 1 1 a c1 c2 c3 c4 c5 c6 d1 d2 d3 j1 j2 j3 
  //   video memory
endmodule

module alu4bit (
  input  no,
  input  f,
  input  zx,
  input  nx,
  input  in_5,
  input  in_6,
  input  in_7,
  input  in_8,
  input  zy,
  input  ny,
  input  in_11,
  input  in_12,
  input  in_13,
  input  in_14,
  output [15:0] o,
  output out_16,
  output zr,
  output ng
);

  wire and_1_out, and_2_out, and_3_out, and_4_out, and_5_out, and_6_out, and_7_out, and_8_out, not_1_out,
       not_2_out, not_5_out, xor_1_out, xor_2_out, xor_3_out, xor_4_out, xor_5_out, xor_6_out, xor_7_out,
       xor_8_out;
  wire [15:0] adder16_1_o, and_9_out, and_10_out, and_11_out, bit_extender_1_out, demultiplexer_1_out0,
       demultiplexer_1_out1, demultiplexer_2_out0, demultiplexer_2_out1, not_3_out, not_4_out, or_1_out,
       undriven, undriven_2, undriven_3, undriven_4, undriven_5, undriven_6, xor_9_out, xor_10_out;

  not not_1 (not_1_out, zx);
  not not_2 (not_2_out, zy);
  and and_1 (and_1_out, not_1_out, in_7);
  and and_2 (and_2_out, not_1_out, in_8);
  and and_3 (and_3_out, not_2_out, in_13);
  and and_4 (and_4_out, not_2_out, in_14);
  and and_5 (and_5_out, not_1_out, in_5);
  and and_6 (and_6_out, not_1_out, in_6);
  and and_7 (and_7_out, not_2_out, in_11);
  and and_8 (and_8_out, not_2_out, in_12);
  xor xor_1 (xor_1_out, and_1_out, nx);
  xor xor_2 (xor_2_out, and_2_out, nx);
  xor xor_3 (xor_3_out, and_3_out, ny);
  xor xor_4 (xor_4_out, and_4_out, ny);
  xor xor_5 (xor_5_out, and_5_out, nx);
  xor xor_6 (xor_6_out, and_6_out, nx);
  xor xor_7 (xor_7_out, and_7_out, ny);
  xor xor_8 (xor_8_out, and_8_out, ny);
  assign not_3_out = ~undriven_3;  // NOT_Gate not_3, 16 bits wide
  assign and_9_out = not_3_out & undriven;  // AND_Gate and_9, 16 bits wide
  assign not_4_out = ~undriven_4;  // NOT_Gate not_4, 16 bits wide
  assign and_10_out = not_4_out & undriven_2;  // AND_Gate and_10, 16 bits wide
  assign xor_9_out = undriven_5 ^ and_9_out;  // XOR_Gate xor_9, 16 bits wide
  assign xor_10_out = undriven_6 ^ and_10_out;  // XOR_Gate xor_10, 16 bits wide
  not not_5 (not_5_out, f);
  Demultiplexer #(.width(16)) demultiplexer_1 (
    .out0(demultiplexer_1_out0), .out1(demultiplexer_1_out1), .in(xor_9_out), .sel(not_5_out));
  Demultiplexer #(.width(16)) demultiplexer_2 (
    .out0(demultiplexer_2_out0), .out1(demultiplexer_2_out1), .in(xor_10_out), .sel(not_5_out));
  assign and_11_out = demultiplexer_1_out1 & demultiplexer_2_out1;  // AND_Gate and_11, 16 bits wide
  adder16 adder16_1 (.a(demultiplexer_1_out0), .b(demultiplexer_2_out0), .o(adder16_1_o));
  assign bit_extender_1_out = {{15{no}}, no};  // Bit_Extender bit_extender_1
  assign or_1_out = adder16_1_o | and_11_out;  // OR_Gate or_1, 16 bits wide
  assign {ng, o[14:0]} = bit_extender_1_out ^ or_1_out;  // XOR_Gate xor_11, 16 bits wide
  not not_6 (zr, out_16);
  or16out1 or16out1_1 (.in_1({ng, o[14:0]}), .out_2(out_16));

  assign o[15] = ng;

  // Notes on the sheet:
  //   x+y
  //   x&y
endmodule
